# Fritzing sketch SensorShirt (saved by Fritzing 0.9.1b)
circuit board: 3.84246cm x 5.93555cm
breadboards: 1

parts:
  Teensy_3_1 = Teensy 3.1
  S1 = Pushbutton [package="[THT]"]
  R1 = Resistor [tolerance=±5% resistance=10k package=THT]
  R2 = Resistor [tolerance=±5% resistance=100 package=THT]
  R3 = Resistor [tolerance=±5% resistance=100 package=THT]
  R4 = Resistor [tolerance=±5% resistance=100 package=THT]
  R5 = Resistor [tolerance=±5% resistance=100 package=THT]
  R6 = Resistor [tolerance=±5% resistance=100 package=THT]
  R7 = Resistor [tolerance=±5% resistance=100 package=THT]
  R8 = Resistor [tolerance=±5% resistance=100 package=THT]
  R9 = Resistor [tolerance=±5% resistance=100 package=THT]
  R10 = Resistor [tolerance=±5% resistance=100 package=THT]
  R11 = Resistor [tolerance=±5% resistance=100 package=THT]

nets:
  N1: Teensy_3_1.GND, R1.Pin_0, R3.Pin_1, R5.Pin_1, R7.Pin_1, R9.Pin_1, R11.Pin_1
  N2: Teensy_3_1.D0, Teensy_3_1.3V3, S1.Pin_1, S1.Pin_2
  N3: Teensy_3_1.A0/D14, R8.Pin_1, R9.Pin_0
  N4: Teensy_3_1.A1/D15, R10.Pin_1, R11.Pin_0
  N5: Teensy_3_1.A2/D16, R6.Pin_1, R7.Pin_0
  N6: Teensy_3_1.A3/D17, R4.Pin_1, R5.Pin_0
  N7: Teensy_3_1.A4/D18, R2.Pin_1, R3.Pin_0
  N8: S1.Pin_3, S1.Pin_4, R1.Pin_1
